# Fritzing sketch SchnapsOMeter (saved by Fritzing 0.8.7b)
circuit board: 6.49994cm x 1.59985cm
breadboards: 2

parts:
  XTAL2 = Crystal [frequency="16 Mhz" package=THT]
  J6 = female pin header, 14 pins [form="♀ (female rounded)"]
  J7 = female pin header, 14 pins [form="♀ (female rounded)"]
  U4 = atmega168 [package=dip]
  C10 = Ceramic Capacitor [capacitance=22pF package="100 mil [THT, multilayer]"]
  C7 = Ceramic Capacitor [capacitance=22pF package="100 mil [THT, multilayer]"]
  U5 = GAS_SENSOR [package=mq-3]
  J9 = female pin header, 3 pins [form="♀ (female)"]
  J10 = female pin header, 2 pins [form="♀ (female)"]
  R1 = Resistor [tolerance=±5% resistance=10k package=THT]
  R2 = Resistor [tolerance=±5% resistance=220 package=THT]
  LED1 = LED - 3mm [color="Red (633nm)" package="3 mm [THT]"]

nets:
  N1: XTAL2.pin_0, J6.pin9, U4.XLAT1, C10.1
  N2: XTAL2.pin_1, J6.pin10, U4.XLAT2, C7.0
  N3: J6.pin1, U4.RESET
  N4: J6.pin2, U4.D0_(RX)
  N5: J6.pin3, U4.D1_(TX)
  N6: J6.pin4, U4.D2
  N7: J6.pin5, U4.D3_(PWM)
  N8: J6.pin6, U4.D4
  N9: J6.pin7, J7.pin8, J7.pin9, U4.VCC, U4.AVCC, U4.AREF, U5.A1, U5.H1, J9.pin3, J10.pin1, LED1.anode
  N10: J6.pin8, J7.pin7, U4.GND, C10.0, C7.1, U5.H2, J9.pin1, J10.pin2, R1.Pin_1, R2.Pin_1
  N11: J6.pin11, U4.D5_(PWM)
  N12: J6.pin12, U4.D6_(PWM)
  N13: J6.pin13, U4.D7
  N14: J6.pin14, U4.D8
  N15: J7.pin1, U4.A5
  N16: J7.pin2, U4.A4
  N17: J7.pin3, U4.A3
  N18: J7.pin4, U4.A2
  N19: J7.pin5, U4.A1
  N20: J7.pin6, U4.A0, U5.B1, R1.Pin_0
  N21: J7.pin10, U4.D13
  N22: J7.pin11, U4.D12
  N23: J7.pin12, U4.D11_(PWM)
  N24: J7.pin13, U4.D10_(PWM)
  N25: J7.pin14, U4.D9_(PWM), J9.pin2
  N26: R2.Pin_0, LED1.cathode

notes:
  This is a breadboard Arduino without an FTDI chip. You can program the chip with a USB-Serial breakout board, by using an external programmer or by programming the MCU in an Arduino board and then popping it into this circuit. The power source should be at least 7 VDC. Related example: http://itp.nyu.edu/physcomp/Tutorials/ArduinoBreadboard
  D8
  D7
  D6
  D5
  D2
  D1
  RES
  D0
  GND
  D3
  VCC
  D4
  D13
  D9
  Aref
  D12
  Avcc
  D10
  D11
  A5
  A2
  A4
  A0
  A3
  A1
  DI
  5V+ IN
  fritzing.org/
  schnapsometer
  MQ3
